# Fritzing sketch fritzing_diagram (saved by Fritzing 0.9.2b)
breadboards: 1

parts:
  U1 = attiny85 [package=dip]
  LED1 = LED - 5mm [color="Red (633nm)" package="5 mm [THT]"]
  R1 = Photocell (LDR) [package=THT]
  R2 = Resistor [tolerance=±5% resistance=220 package=THT]
  R3 = Resistor [tolerance=±5% resistance=220 package=THT]
  VCC1 = Battery

nets:
  N1: U1.Pin_2, R2.Pin_1
  N2: U1.Pin_3, R1.pin_0, R3.Pin_0
  N3: U1.Pin_4, LED1.cathode, R1.pin_1, VCC1.-
  N4: U1.Pin_8, R3.Pin_1, VCC1.+
  N5: LED1.anode, R2.Pin_0
